# Fritzing sketch Nano-NumberAttack8 (saved by Fritzing 1.0.6)
breadboards: 3
perfboards: 1

parts:
  S1 = Momentary Switch 6mm 2pin
  S2 = Momentary Switch 6mm 2pin
  SG1 = Buzzer 12mm [part_number=COM-07950 package=buzzer-12mm-ns]
  A1 = Hiletgo 8digit led display

nets:
  N1: S1.2, S2.2, SG1.2, A1.Pin_2, A1.Pin_9

notes:
  8桁 LEDモジュール
  ミニブレッドボード 3個
  タクトスイッチ #1
  パッシブブザー
  タクトスイッチ #2
  NANO V3 SuperMini
  USB 端子が下側になるように取り付ける
  ⊕印が下側になるように取り付ける

custom parts:
  Momentary Switch 6mm 2pin: Momentary Switch 6mm 2 pin Button commonly used for reset or general input.
  Buzzer 12mm: Buzzer 12mm Spark Fun Electronics SKU : Comp-Buzzer Through hole This is a small 12mm round speaker that operates around the audible 2kHz range. You can use these speakers to create simple music or user interfaces. This is not a true piezoelectric speaker but behaves similarly. Instead of a piezoelectric crystal that vibrates with an electric current, this tiny speaker uses an electromagnet to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
  Hiletgo 8digit led display: MAX7219 is an integrated serial input / output common-cathode display driver, which connects your microprocessor to a 7-segment digital LED display with 8 digits.
